# Fritzing sketch Amiacs Arcade (saved by Fritzing 0.9.3b)

parts:
  Part1 = 24-Channel 12-bit PWM LED Driver - SPI [part_number=1429]
  Part2 = Arduino Nano (Rev3.0) (ICSP)
  D1 = Rectifier Diode [part_number=1N4001 package="300 mil [THT]"]
  J6 = single row smd female pin header, 2 pins [form="♀ (female)"]
  J2 = single row smd male pin header, 2 pins [form="♂ (male)"]
  J3 = double row smd male pin header, 2 pins [form="♂ (male)"]
  JST_SM_M/F = single row smd female pin header, 2 pins [form="♀ (female)"]
  J7 = double row smd male pin header, 2 pins [form="♂ (male)"]
  J8 = single row smd female pin header, 2 pins [form="♀ (female)"]
  J9 = double row smd male pin header, 4 pins [form="♂ (male)"]
  J10 = single row smd female pin header, 4 pins [form="♀ (female)"]
  J11 = double row smd male pin header, 2 pins [form="♂ (male)"]
  J12 = single row smd female pin header, 2 pins [form="♀ (female)"]
  B = Pushbutton [package=THT]
  K12 = female pin header, 3 pins [form="♀ (female)"]
  LED2 = LED - 5mm [color="Blue (525nm)" package="5 mm [THT]"]
  Player_1 = USB connector [package=THT]  # not connected
  K11 = female pin header, 3 pins [form="♀ (female)"]
  ST = female pin header, 3 pins [form="♀ (female)"]
  SE = female pin header, 3 pins [form="♀ (female)"]
  R1 = female pin header, 3 pins [form="♀ (female)"]
  L1 = female pin header, 3 pins [form="♀ (female)"]
  R2 = female pin header, 3 pins [form="♀ (female)"]
  L2 = female pin header, 3 pins [form="♀ (female)"]
  K4 = female pin header, 3 pins [form="♀ (female)"]
  K3 = female pin header, 3 pins [form="♀ (female)"]
  K2 = female pin header, 3 pins [form="♀ (female)"]
  K1 = female pin header, 3 pins [form="♀ (female)"]
  A = Pushbutton [package=THT]
  LED3 = LED - 5mm [color="Blue (525nm)" package="5 mm [THT]"]
  L1_2 = Pushbutton [package=THT]
  LED4 = LED - 5mm [color="Blue (525nm)" package="5 mm [THT]"]
  R1_2 = Pushbutton [package=THT]
  LED5 = LED - 5mm [color="Blue (525nm)" package="5 mm [THT]"]
  Y = Pushbutton [package=THT]
  L2_2 = Pushbutton [package=THT]
  X = Pushbutton [package=THT]
  R2_2 = Pushbutton [package=THT]
  LED6 = LED - 5mm [color="Blue (525nm)" package="5 mm [THT]"]
  LED7 = LED - 5mm [color="Blue (525nm)" package="5 mm [THT]"]
  LED8 = LED - 5mm [color="Blue (525nm)" package="5 mm [THT]"]
  LED9 = LED - 5mm [color="Blue (525nm)" package="5 mm [THT]"]
  EXIT = Pushbutton [package=THT]
  LED10 = LED - 5mm [color="Yellow (595nm)" package="5 mm [THT]"]
  SELECT = Pushbutton [package=THT]
  START = Pushbutton [package=THT]
  LED11 = LED - 5mm [color="Blue (525nm)" package="5 mm [THT]"]
  LED12 = LED - 5mm [color="Blue (525nm)" package="5 mm [THT]"]
  HOTKEY = Pushbutton [package=THT]
  LED13 = LED - 5mm [color="Yellow (595nm)" package="5 mm [THT]"]
  JOY1 = Adafruit Arcade Joystick  # not connected
  D3 = Rectifier Diode [part_number=1N4001 package="300 mil [THT]"]

nets:
  N1: Part1.LAT, J9.pin1
  N2: Part1.OE, J9.pin2
  N3: Part1.CLK, J9.pin3
  N4: Part1.DIN, J9.pin4
  N5: Part1.GND, J7.pin2, J11.pin1
  N6: Part1.+24V, J7.pin1
  N7: Part1.PWM0, LED2.anode
  N8: Part1.PWM1, LED3.anode
  N9: Part1.PWM2, LED6.anode
  N10: Part1.PWM3, LED9.anode
  N11: Part1.PWM4, LED8.anode
  N12: Part1.PWM5, LED7.anode
  N13: Part1.PWM6, LED4.anode
  N14: Part1.PWM7, LED5.anode
  N15: Part1.PWM8, LED12.anode
  N16: Part1.PWM9, LED11.anode
  N17: Part1.PWM10, LED10.anode
  N18: Part1.PWM11, LED13.anode
  N19: Part2.D8, J10.pin3
  N20: Part2.D10, J10.pin4
  N21: Part2.D12/MISO, J10.pin1
  N22: Part2.GND, J12.pin2
  N23: Part2.D13/SCK, J10.pin2
  N24: D1.cathode, JST_SM_M/F.pin2, D3.cathode
  N25: D1.anode, J6.pin2, J3.pin1
  N26: J6.pin1, J2.pin2, J3.pin2, JST_SM_M/F.pin1
  N27: J2.pin1, D3.anode
  N28: J8.pin1, K11.pin3
  N29: J8.pin2, K11.pin1, EXIT.leg0, LED10.cathode
  N30: B.leg0, LED2.cathode, K1.pin1
  N31: B.leg1, K1.pin2
  N32: K12.pin1, HOTKEY.leg0, LED13.cathode
  N33: K12.pin2, HOTKEY.leg1
  N34: K11.pin2, EXIT.leg1
  N35: ST.pin1, START.leg0, LED11.cathode
  N36: ST.pin2, START.leg1
  N37: SE.pin1, SELECT.leg0, LED12.cathode
  N38: SE.pin2, SELECT.leg1
  N39: R1.pin1, R1_2.leg0, LED5.cathode
  N40: R1.pin2, R1_2.leg1
  N41: L1.pin1, L1_2.leg0, LED4.cathode
  N42: L1.pin2, L1.pin3, L1_2.leg1
  N43: R2.pin1, R2_2.leg0, LED7.cathode
  N44: R2.pin2, R2_2.leg1
  N45: L2.pin1, L2_2.leg0, LED8.cathode
  N46: L2.pin2, L2_2.leg1
  N47: K4.pin1, X.leg0, LED9.cathode
  N48: K4.pin2, X.leg1
  N49: K3.pin1, Y.leg0, LED6.cathode
  N50: K3.pin2, Y.leg1
  N51: K2.pin1, A.leg0, LED3.cathode
  N52: K2.pin2, A.leg1

notes:
  The V+ and GND wire colors coming from the controllers are opposite. This connection will look wrong.
  These diodes are used to keep the voltage from going from one controller to the other.
  Most components are representations. The properties do not reflect the actual part.
  The pushbuttons and LEDs represent the arcade buttons.
  The TLC5947 is upside down in the physical panel.

custom parts:
  24-Channel 12-bit PWM LED Driver - SPI: This breakout board for the TLC5947 PWM driver chip can control 24 separate channels of 12-bit PWM output. Designed (and ideal) for LED control, this board is NOT good for driving servos. Only three "SPI" pins are required to send data (our Arduino library shows how to to use any digital microcontroller pins). Best of all, the design is completely chainable. As long as there's enough power for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
